// Logisim project ArquivoCirc.circ as structural Verilog: 1 circuit, main circuit main
module main (
  input  in_1,
  input  in_2,
  input  in_3,
  input  in_4,
  input  in_5,
  input  in_6,
  input  in_7,
  input  in_8,
  input  in_9,
  input  in_10,
  input  in_11,
  input  in_12,
  input  in_13,
  input  in_14,
  input  in_15,
  input  in_16,
  input  in_17,
  input  in_18,
  output out_19,
  output out_20,
  output out_21,
  output out_22
);

  wire AND_2_out, AND_3_out, AND_out, NAND_2_out, NAND_out, NOR_out, OR_2_out, OR_3_out, OR_out;

  or OR (OR_out, in_1, in_2);
  and AND (AND_out, in_6, in_7, in_8);
  or AND_2 (AND_2_out, in_11, in_12);
  or AND_3 (AND_3_out, in_13, in_14);
  nand NAND (NAND_out, in_15, in_16);
  nor NOR (NOR_out, in_17, in_18);
  or OR_2 (OR_2_out, OR_out, in_3);
  and AND_4 (out_21, AND_2_out, AND_3_out);
  or OR_3 (OR_3_out, OR_2_out, in_4);
  and AND_5 (out_20, AND_out, in_9, in_10);
  nand NAND_2 (NAND_2_out, NAND_out, in_17);
  or OR_4 (out_19, OR_3_out, in_5);
  xor XOR (out_22, NAND_2_out, NOR_out);
endmodule
