// Logisim project ArquivoCirc.circ as structural Verilog: 1 circuit, main circuit main
module main (
  input  A,
  input  C,
  input  D,
  output out_4
);

  wire AND_out, NOT_2_out, NOT_out, OR_out;

  and AND (AND_out, A, D);
  not NOT (NOT_out, D);
  not NOT_2 (NOT_2_out, C);
  or OR (OR_out, AND_out, NOT_out);
  and AND_2 (out_4, OR_out, NOT_2_out);
endmodule
