// Logisim project arquivo-circ.circ as structural Verilog: 1 circuit, main circuit main
module main (
  input  A,
  input  B,
  input  C__IN,
  input  A_2,
  input  B_2,
  input  C__IN_2,
  output out_7,
  output out_8
);

  wire AND_2_out, AND_3_out, AND_4_out, AND_5_out, AND_out, OR_out, XOR_out;

  xor XOR (XOR_out, B_2, C__IN_2);
  and AND (AND_out, B, C__IN);
  and AND_2 (AND_2_out, A_2, XOR_out);
  and AND_3 (AND_3_out, B_2, C__IN_2);
  or OR (OR_out, AND_out, ~B);  // OR_Gate
  or OR_2 (out_8, AND_2_out, AND_3_out);
  and AND_4 (AND_4_out, A, OR_out);
  and AND_5 (AND_5_out, ~A, B, ~C__IN);  // AND_Gate
  or OR_3 (out_7, AND_4_out, AND_5_out);
endmodule
