// Logisim project circuito-sirene.circ as structural Verilog: 1 circuit, main circuit main
module main (
  input  K,
  input  L,
  input  M,
  input  N,
  output TOCAR
);

  wire AND_2_out, AND_out;

  and AND (AND_out, K, L);
  and AND_2 (AND_2_out, M, L, N);
  or OR (TOCAR, AND_out, AND_2_out);
endmodule
