// Logisim project Circ.circ as structural Verilog: 1 circuit, main circuit main
module main (
  input  in_1,
  input  in_2,
  input  in_3,
  input  in_4,
  input  in_5,
  input  in_6,
  output Q,
  output Q_prime,
  output Q_2,
  output Q_prime_2,
  output Q_3,
  output Q_prime_3,
  output Q_4,
  output Q_prime_4
);

  wire clock_1_out, clock_2_out, clock_3_out, clock_4_out;

  Clock clock_1 (.out(clock_1_out));
  Clock clock_2 (.out(clock_2_out));
  Clock clock_3 (.out(clock_3_out));
  Clock clock_4 (.out(clock_4_out));
  T_Flip_Flop t_ff_1 (.clk(clock_1_out), .T(in_1), .Q(Q), .Qn(Q_prime));  // open: preset, reset, en
  D_Flip_Flop d_ff_1 (.clk(clock_2_out), .D(in_2), .Q(Q_2), .Qn(Q_prime_2));  // open: preset, en, reset
  J_K_Flip_Flop j_k_ff_1 (.J(in_3), .clk(clock_3_out), .K(in_4), .Q(Q_3), .Qn(Q_prime_3));  // open: preset, en, reset
  S_R_Flip_Flop s_r_ff_1 (.S(in_5), .clk(clock_4_out), .R(in_6), .Q(Q_4), .Qn(Q_prime_4));  // open: preset, reset, en
endmodule
