// Logisim project arq-cirq.circ as structural Verilog: 1 circuit, main circuit main
module main (
  input  in_1,
  input  in_2
);

  wire AND_out, clock_1_out;
  wire [0:0] j_k_ff_5_q;
  wire [3:0] j_k_ff_1_q;

  Clock clock_1 (.out(clock_1_out));
  J_K_Flip_Flop #(.trigger("falling")) j_k_ff_1 (
    .J(in_2), .clk(clock_1_out), .K(in_2), .Q(j_k_ff_1_q[0]), .reset(AND_out));  // open: Qn, preset, en
  J_K_Flip_Flop #(.trigger("falling")) j_k_ff_2 (
    .J(in_2), .clk(j_k_ff_1_q[0]), .K(in_2), .Q(j_k_ff_1_q[1]), .reset(AND_out));  // open: Qn, preset, en
  J_K_Flip_Flop #(.trigger("falling")) j_k_ff_3 (
    .J(in_2), .clk(j_k_ff_1_q[1]), .K(in_2), .Q(j_k_ff_1_q[2]), .reset(AND_out));  // open: Qn, preset, en
  J_K_Flip_Flop #(.trigger("falling")) j_k_ff_4 (
    .J(in_2), .clk(j_k_ff_1_q[2]), .K(in_2), .Q(j_k_ff_1_q[3]), .reset(AND_out));  // open: Qn, preset, en
  and AND (AND_out, j_k_ff_5_q[0], j_k_ff_1_q[3], j_k_ff_1_q[2], ~j_k_ff_1_q[1], ~j_k_ff_1_q[0]);  // AND_Gate
  J_K_Flip_Flop #(.trigger("falling")) j_k_ff_5 (
    .J(in_2), .clk(j_k_ff_1_q[3]), .K(in_2), .Q(j_k_ff_5_q[0]), .reset(AND_out));  // open: Qn, preset, en
  Hex_Digit_Display hex_digit_display_1 (.value({{3{in_1}}, j_k_ff_5_q[0]}));  // open: dp
  Hex_Digit_Display hex_digit_display_2 (.value(j_k_ff_1_q));  // open: dp
endmodule
