// Logisim project circuito(2).circ as structural Verilog: 1 circuit, main circuit main
module main (
  input  in_1,
  input  in_2
);

  wire A_2_q, A_2_qn, A_B_prime_D_out, A_C_out, A_C_prime_D_prime_out, A_prime_B_prime_out, A_prime_D_out,
       A_q, AC_prime_B_prime_C_prime_out, AC_prime_out, B_CD_prime_out, B_prime_C_prime_out, B_prime_D_out,
       B_q, B_qn, BC_out, C_2_q, C_2_qn, C_prime_D_prime_out, C_q, CD_out, CD_prime_out, clock_1_out,
       clock_2_out, D_2_q, D_2_qn, D_q, j_k_ff_1_q;

  Clock clock_1 (.out(clock_1_out));
  and BC (BC_out, C_q, j_k_ff_1_q);
  and C_prime_D_prime (C_prime_D_prime_out, ~D_2_q, ~C_2_q);  // AND_Gate
  Clock clock_2 (.out(clock_2_out));
  and CD (CD_out, D_q, C_q);
  J_K_Flip_Flop A (.J(BC_out), .clk(clock_1_out), .K(j_k_ff_1_q), .Q(A_q));  // open: Qn, preset, en, reset
  or A_C (A_C_out, A_q, C_q);
  or A_C_prime_D_prime (A_C_prime_D_prime_out, A_2_q, C_prime_D_prime_out);
  J_K_Flip_Flop A_2 (
    .J(C_prime_D_prime_out), .clk(clock_2_out), .K(B_qn), .Q(A_2_q), .Qn(A_2_qn));  // open: preset, en, reset
  or A_B_prime_D (A_B_prime_D_out, A_q, B_prime_D_out);
  J_K_Flip_Flop j_k_ff_1 (.J(CD_out), .clk(clock_1_out), .K(A_C_out), .Q(j_k_ff_1_q));  // open: Qn, preset, en, reset
  and A_prime_D (A_prime_D_out, ~A_q, D_q);  // AND_Gate
  J_K_Flip_Flop B (
    .J(A_C_prime_D_prime_out), .clk(clock_2_out), .K(C_2_qn), .Q(B_q), .Qn(B_qn));  // open: preset, en, reset
  and B_prime_D (B_prime_D_out, ~j_k_ff_1_q, D_q);  // AND_Gate
  J_K_Flip_Flop C (.J(A_prime_D_out), .clk(clock_1_out), .K(A_B_prime_D_out), .Q(C_q));  // open: Qn, preset, en, reset
  and AC_prime (AC_prime_out, A_q, ~C_q);  // AND_Gate
  and B_prime_C_prime (B_prime_C_prime_out, ~j_k_ff_1_q, ~C_q);  // AND_Gate
  J_K_Flip_Flop C_2 (
    .J(B_q), .clk(clock_2_out), .K(B_CD_prime_out), .Q(C_2_q), .Qn(C_2_qn));  // open: preset, en, reset
  or B_CD_prime (B_CD_prime_out, B_q, CD_prime_out);
  and CD_prime (CD_prime_out, C_2_q, D_2_qn);
  J_K_Flip_Flop D (
    .J(in_1), .clk(clock_1_out), .K(AC_prime_B_prime_C_prime_out), .Q(D_q));  // open: Qn, preset, en, reset
  or AC_prime_B_prime_C_prime (AC_prime_B_prime_C_prime_out, AC_prime_out, B_prime_C_prime_out);
  and A_prime_B_prime (A_prime_B_prime_out, A_2_qn, B_qn);
  J_K_Flip_Flop D_2 (
    .J(in_2), .clk(clock_2_out), .K(A_prime_B_prime_out), .Q(D_2_q), .Qn(D_2_qn));  // open: preset, en, reset
endmodule
