// Logisim project circuito.circ as structural Verilog: 1 circuit, main circuit main
module main (
  input  ALTERNAR
);

  wire A_B_prime_D_out, A_C_out, A_C_prime_D_prime_out, A_prime_B_prime_out, A_prime_D_out, A_q, A_qn,
       AC_prime___B_prime_C_prime_out, AC_prime_out, B_CD_prime_out, B_prime_C_prime_out, B_prime_D_out, B_q,
       B_qn, BC_out, C_prime_D_prime_out, C_q, C_qn, CD_out, CD_prime_out, clock_1_out, D_q, D_qn,
       multiplexer_1_out, multiplexer_2_out, multiplexer_3_out, multiplexer_4_out, multiplexer_5_out,
       multiplexer_6_out, multiplexer_7_out, multiplexer_8_out, RESET_out;

  Clock clock_1 (.out(clock_1_out));
  Button RESET (.out(RESET_out));
  Multiplexer #(.enable("false")) multiplexer_1 (
    .in0(BC_out), .in1(C_prime_D_prime_out), .out(multiplexer_1_out), .sel(ALTERNAR));
  Multiplexer #(.enable("false")) multiplexer_2 (.in0(B_q), .in1(B_qn), .out(multiplexer_2_out), .sel(ALTERNAR));
  and BC (BC_out, B_q, C_q);
  and C_prime_D_prime (C_prime_D_prime_out, C_qn, D_qn);
  J_K_Flip_Flop A (
    .J(multiplexer_1_out), .clk(clock_1_out), .K(multiplexer_2_out), .Q(A_q), .Qn(A_qn), .reset(RESET_out));  // open: preset, en
  or A_C_prime_D_prime (A_C_prime_D_prime_out, A_q, C_prime_D_prime_out);
  or A_C (A_C_out, A_q, C_q);
  Multiplexer #(.enable("false")) multiplexer_3 (
    .in0(CD_out), .in1(A_C_prime_D_prime_out), .out(multiplexer_3_out), .sel(ALTERNAR));
  Multiplexer #(.enable("false")) multiplexer_4 (.in0(A_C_out), .in1(C_qn), .out(multiplexer_4_out), .sel(ALTERNAR));
  and A_prime_B_prime (A_prime_B_prime_out, A_qn, B_qn);
  J_K_Flip_Flop B (
    .J(multiplexer_3_out), .clk(clock_1_out), .K(multiplexer_4_out), .Q(B_q), .Qn(B_qn), .reset(RESET_out));  // open: preset, en
  and A_prime_D (A_prime_D_out, A_qn, D_q);
  Multiplexer #(.enable("false")) multiplexer_5 (
    .in0(A_prime_D_out), .in1(B_q), .out(multiplexer_5_out), .sel(ALTERNAR));
  Multiplexer #(.enable("false")) multiplexer_6 (
    .in0(A_B_prime_D_out), .in1(B_CD_prime_out), .out(multiplexer_6_out), .sel(ALTERNAR));
  or B_CD_prime (B_CD_prime_out, B_q, CD_prime_out);
  or A_B_prime_D (A_B_prime_D_out, A_q, B_prime_D_out);
  and B_prime_D (B_prime_D_out, B_qn, D_q);
  J_K_Flip_Flop C (
    .J(multiplexer_5_out), .clk(clock_1_out), .K(multiplexer_6_out), .Q(C_q), .Qn(C_qn), .reset(RESET_out));  // open: preset, en
  and CD_prime (CD_prime_out, C_q, D_qn);
  and CD (CD_out, C_q, D_q);
  and AC_prime (AC_prime_out, A_q, C_qn);
  and B_prime_C_prime (B_prime_C_prime_out, B_qn, C_qn);
  Multiplexer #(.enable("false")) multiplexer_7 (.in0(1'b1), .in1(1'b1), .out(multiplexer_7_out), .sel(ALTERNAR));
  Multiplexer #(.enable("false")) multiplexer_8 (
    .in0(AC_prime___B_prime_C_prime_out), .in1(A_prime_B_prime_out), .out(multiplexer_8_out), .sel(ALTERNAR));
  or AC_prime___B_prime_C_prime (AC_prime___B_prime_C_prime_out, AC_prime_out, B_prime_C_prime_out);
  J_K_Flip_Flop D (
    .J(multiplexer_7_out), .clk(clock_1_out), .K(multiplexer_8_out), .Q(D_q), .Qn(D_qn), .reset(RESET_out));  // open: preset, en
  LED Crescente___Decrescente (.in(ALTERNAR));
endmodule
